// Logisim project smips.circ as structural Verilog
module Board (
);

  wire CLK, HALT, MEM_WE, RESET, TTY_WE;
  wire [3:0] MEM_BE;
  wire [6:0] TTY_DATA;
  wire [31:0] MEM_ADDR, MEM_RDATA, MEM_WDATA;

  Clock Reloj (.out(CLK));
  Button u_Reset (.out(RESET));
  CPU cpu_1 (
    .CLK(CLK), .RESET(RESET), .MEM_RDATA(MEM_RDATA), .MEM_ADDR(MEM_ADDR), .MEM_WDATA(MEM_WDATA),
    .MEM_BE(MEM_BE), .MEM_WE(MEM_WE), .TTY_DATA(TTY_DATA), .TTY_WE(TTY_WE), .HALT(HALT));
  TTY #(.cols(48), .rows(12)) tty_1 (.data(TTY_DATA), .clk(CLK), .we(TTY_WE), .clr(RESET));
  Memory memory_1 (.CLK(CLK), .ADDR(MEM_ADDR), .WDATA(MEM_WDATA), .BE(MEM_BE), .WE(MEM_WE), .RDATA(MEM_RDATA));
  LED u_Halt (.in(HALT));

  // Notes on the sheet:
  //   S-MIPS | Board
  //   No modificar: la CPU se implementa dentro del subcircuito CPU.
endmodule

module CPU (
  input  CLK,
  input  RESET,
  input  [31:0] MEM_RDATA,
  output [31:0] MEM_ADDR,
  output [31:0] MEM_WDATA,
  output [3:0] MEM_BE,
  output MEM_WE,
  output [6:0] TTY_DATA,
  output TTY_WE,
  output HALT
);


  // Notes on the sheet:
  //   CPU S-MIPS: implementar aqui
  //   No cambiar nombres, anchos ni sentido de los pines: la placa depende de ellos.
endmodule

module Memory (
  input  CLK,
  input  [31:0] ADDR,
  input  [31:0] WDATA,
  input  [3:0] BE,
  input  WE,
  output [31:0] RDATA
);

  RAM #(.addrWidth(12), .asyncread("true"), .byteenables("byteEnables"), .dataWidth(32), .\type ("nonvolatile")) Main_Memory (
    .addr(ADDR[13:2]), .we(WE), .oe(1'b1), .clk(CLK), .din(WDATA), .dout(RDATA), .be3(BE[3]), .be2(BE[2]),
    .be1(BE[1]), .be0(BE[0]));

  // Other names for the same wires on the sheet: A[11:0] = ADDR[13:2]

  // Notes on the sheet:
  //   Memoria unificada: 4096 palabras de 32 bits (16 KiB), little-endian
  //   Lectura combinacional; escritura en el flanco de subida de CLK con WE=1, solo en los bytes con BE=1.
  //   Se usan los bits 13..2 de ADDR; los demas se ignoran (el espacio se repite cada 16 KiB).
endmodule

module ALU (
  input  [31:0] A,
  input  [31:0] B,
  input  [2:0] ALUControl,
  input  [4:0] Shamt,
  output [31:0] Result,
  output Zero
);

  wire comparator_1_lt;
  wire [31:0] adder_1_out, and_1_out, bit_extender_1_out, or_1_out, shifter_1_out, shifter_2_out,
       shifter_3_out, subtractor_1_out;

  Adder #(.width(32)) adder_1 (.a(A), .b(B), .out(adder_1_out));  // open: cin, cout
  Subtractor #(.width(32)) subtractor_1 (.a(A), .b(B), .out(subtractor_1_out));  // open: bin, bout
  Comparator #(.width(32)) comparator_1 (.a(A), .b(B), .lt(comparator_1_lt));  // open: gt, eq
  Shifter #(.width(32)) shifter_1 (.in(B), .\dist (Shamt), .out(shifter_1_out));
  Shifter #(.shift("lr"), .width(32)) shifter_2 (.in(B), .\dist (Shamt), .out(shifter_2_out));
  Shifter #(.width(32)) shifter_3 (.in(B), .\dist (5'b10000), .out(shifter_3_out));
  assign and_1_out = A & B;  // AND_Gate and_1, 32 bits wide
  assign or_1_out = A | B;  // OR_Gate or_1, 32 bits wide
  assign bit_extender_1_out = {{31{1'b0}}, comparator_1_lt};  // Bit_Extender bit_extender_1
  Multiplexer #(.select(3), .width(32)) multiplexer_1 (
    .in0(adder_1_out), .in1(subtractor_1_out), .in2(and_1_out), .in3(or_1_out), .in4(bit_extender_1_out),
    .in5(shifter_1_out), .in6(shifter_2_out), .in7(shifter_3_out), .out(Result), .sel(ALUControl));
  Comparator #(.width(32)) comparator_2 (.a(Result), .b({32{1'b0}}), .eq(Zero));  // open: gt, lt

  // Other names for the same wires on the sheet: ALU[2:0] = ALUControl
endmodule

module Register_File (
  input  [4:0] ReadReg2,
  input  [4:0] WriteReg,
  input  [31:0] WriteData,
  input  RegWrite,
  input  RESET,
  input  [4:0] ReadReg1,
  output [31:0] ReadData1,
  output [31:0] ReadData2
);

  wire [31:0] register_1_q, register_2_q, register_3_q, register_4_q, register_5_q, register_6_q,
       register_7_q, register_8_q, register_9_q, register_10_q, register_11_q, register_12_q, register_13_q,
       register_14_q, register_15_q, register_16_q, register_17_q, register_18_q, register_19_q,
       register_20_q, register_21_q, register_22_q, register_23_q, register_24_q, register_25_q,
       register_26_q, register_27_q, register_28_q, register_29_q, register_31_q, register_32_q,
       register_33_q;

  Clock clock_1 ();  // open: out
  Register #(.width(32)) register_1 (.Q(register_1_q));  // open: D, en, clk, clr
  Register #(.width(32)) register_2 (.Q(register_2_q));  // open: D, en, clk, clr
  Register #(.width(32)) register_3 (.Q(register_3_q));  // open: D, en, clk, clr
  Register #(.width(32)) register_4 (.Q(register_4_q));  // open: D, en, clk, clr
  Register #(.width(32)) register_5 (.Q(register_5_q));  // open: D, en, clk, clr
  Register #(.width(32)) register_6 (.Q(register_6_q));  // open: D, en, clk, clr
  Register #(.width(32)) register_7 (.Q(register_7_q));  // open: D, en, clk, clr
  Register #(.width(32)) register_8 (.Q(register_8_q));  // open: D, en, clk, clr
  Register #(.width(32)) register_9 (.Q(register_9_q));  // open: D, en, clk, clr
  Register #(.width(32)) register_10 (.Q(register_10_q));  // open: D, en, clk, clr
  Register #(.width(32)) register_11 (.Q(register_11_q));  // open: D, en, clk, clr
  Register #(.width(32)) register_12 (.Q(register_12_q));  // open: D, en, clk, clr
  Register #(.width(32)) register_13 (.Q(register_13_q));  // open: D, en, clk, clr
  Register #(.width(32)) register_14 (.Q(register_14_q));  // open: D, en, clk, clr
  Register #(.width(32)) register_15 (.Q(register_15_q));  // open: D, en, clk, clr
  Register #(.width(32)) register_16 (.Q(register_16_q));  // open: D, en, clk, clr
  Register #(.width(32)) register_17 (.Q(register_17_q));  // open: D, en, clk, clr
  Register #(.width(32)) register_18 (.Q(register_18_q));  // open: D, en, clk, clr
  Register #(.width(32)) register_19 (.Q(register_19_q));  // open: D, en, clk, clr
  Register #(.width(32)) register_20 (.Q(register_20_q));  // open: D, en, clk, clr
  Register #(.width(32)) register_21 (.Q(register_21_q));  // open: D, en, clk, clr
  Register #(.width(32)) register_22 (.Q(register_22_q));  // open: D, en, clk, clr
  Register #(.width(32)) register_23 (.Q(register_23_q));  // open: D, en, clk, clr
  Register #(.width(32)) register_24 (.Q(register_24_q));  // open: D, en, clk, clr
  Register #(.width(32)) register_25 (.Q(register_25_q));  // open: D, en, clk, clr
  Register #(.width(32)) register_26 (.Q(register_26_q));  // open: D, en, clk, clr
  Register #(.width(32)) register_27 (.Q(register_27_q));  // open: D, en, clk, clr
  Register #(.width(32)) register_28 (.Q(register_28_q));  // open: D, en, clk, clr
  Register #(.width(32)) register_29 (.Q(register_29_q));  // open: D, en, clk, clr
  Register #(.width(32)) register_30 (.Q(register_29_q));  // open: D, en, clk, clr
  Register #(.width(32)) register_31 (.Q(register_31_q));  // open: D, en, clk, clr
  Register #(.width(32)) register_32 (.Q(register_32_q));  // open: D, en, clk, clr
  Register #(.width(32)) register_33 (.Q(register_33_q));  // open: D, en, clk, clr
  Multiplexer #(.select(5), .width(32)) multiplexer_1 (
    .in0(register_1_q), .in1(register_2_q), .in2(register_3_q), .in3(register_4_q), .in4(register_5_q),
    .in5(register_6_q), .in6(register_7_q), .in7(register_8_q), .in8(register_9_q), .in9(register_10_q),
    .in10(register_11_q), .in11(register_12_q), .in12(register_13_q), .in13(register_14_q),
    .in14(register_15_q), .in15(register_16_q), .in16(register_17_q), .in17(register_18_q),
    .in18(register_19_q), .in19(register_20_q), .in20(register_21_q), .in21(register_22_q),
    .in22(register_23_q), .in23(register_24_q), .in24(register_25_q), .in25(register_26_q),
    .in26(register_27_q), .in27(register_28_q), .in28(register_29_q), .in29(register_31_q),
    .in30(register_32_q), .in31(register_33_q), .out(ReadData1), .sel(ReadReg1));
  Multiplexer #(.select(5), .width(32)) multiplexer_2 (
    .in0(register_1_q), .in1(register_2_q), .in2(register_3_q), .in3(register_4_q), .in4(register_5_q),
    .in5(register_6_q), .in6(register_7_q), .in7(register_8_q), .in8(register_9_q), .in9(register_10_q),
    .in10(register_11_q), .in11(register_12_q), .in12(register_13_q), .in13(register_14_q),
    .in14(register_15_q), .in15(register_16_q), .in16(register_17_q), .in17(register_18_q),
    .in18(register_19_q), .in19(register_20_q), .in20(register_21_q), .in21(register_22_q),
    .in22(register_23_q), .in23(register_24_q), .in24(register_25_q), .in25(register_26_q),
    .in26(register_27_q), .in27(register_28_q), .in28(register_29_q), .in29(register_31_q),
    .in30(register_32_q), .in31(register_33_q), .out(ReadData2), .sel(ReadReg2));

  // Other names for the same wires on the sheet: AB[4:0] = ReadReg1; AC[4:0] = ReadReg2
endmodule
